// Logisim project CPU_circuit.circ as structural Verilog: 1 circuit, main circuit main
module main (
  input  in_1
);

  wire alu_full_section_1_branch_condition, clock_1_out, clock_2_out, Decode_Ctrl_branch_instr,
       Decode_Ctrl_datasrc_mux, Decode_Ctrl_immediate_mux, Decode_Ctrl_jal, Decode_Ctrl_jr,
       Decode_Ctrl_memwr, Decode_Ctrl_wrctrl, main_2_data_value, main_2_write_control;
  wire [2:0] Decode_Ctrl_alu_opcode, Decode_Ctrl_rdsel1, Decode_Ctrl_rdsel2, Decode_Ctrl_wrsel;
  wire [5:0] main_2_output_address;
  wire [7:0] alu_full_section_1_reg_file_data_in, Decode_Ctrl_immediate,
       main_1_connects_to_the_mux_in_regfile, main_2_load_value, main_3_out_4, main_3_out_5, main_3_out_6,
       main_3_out_7, main_3_out_8, main_3_out_9, main_3_out_10, main_3_out_11, registerfile_1_reg1,
       registerfile_1_reg2;
  wire [8:0] Decode_Ctrl_branch_imm;
  wire [11:0] Decode_Ctrl_jumpimm;
  wire [15:0] main_1_connects_to_decoder;

  she_decode_control_main Decode_Ctrl (
    .Data(main_1_connects_to_decoder), .DataSrc_Mux(Decode_Ctrl_datasrc_mux), .MemWr(Decode_Ctrl_memwr),
    .WrCtrl(Decode_Ctrl_wrctrl), .Branch_Instr(Decode_Ctrl_branch_instr),
    .Immediate_Mux(Decode_Ctrl_immediate_mux), .JR(Decode_Ctrl_jr), .JAL(Decode_Ctrl_jal),
    .ALU_Opcode(Decode_Ctrl_alu_opcode), .JumpImm(Decode_Ctrl_jumpimm), .WrSel(Decode_Ctrl_wrsel),
    .Branch_Imm(Decode_Ctrl_branch_imm), .Rdsel1(Decode_Ctrl_rdsel1), .Rdsel2(Decode_Ctrl_rdsel2),
    .Immediate(Decode_Ctrl_immediate));
  // Probe on main_1_connects_to_the_mux_in_regfile
  nazhar_PC_IMEM_main main_1 (
    .Branch_Instruction(Decode_Ctrl_branch_instr), .Jump_Imm_12(Decode_Ctrl_jumpimm),
    .Branch_Imm(Decode_Ctrl_branch_imm), .JR(Decode_Ctrl_jr), .JAL(Decode_Ctrl_jal),
    .Branch_Cond(alu_full_section_1_branch_condition), .Reg_1(registerfile_1_reg1), .Reset_Button(in_1),
    .Connects_to_the_mux_in_RegFile(main_1_connects_to_the_mux_in_regfile),
    .Connects_to_Decoder(main_1_connects_to_decoder));
  Clock clock_1 (.out(clock_1_out));
  registerfile registerfile_1 (
    .ALU_DMEM_Input(alu_full_section_1_reg_file_data_in),
    .JAL_PC_input(main_1_connects_to_the_mux_in_regfile), .JAL(Decode_Ctrl_jal), .Wrctl(Decode_Ctrl_wrctrl),
    .Wrsel(Decode_Ctrl_wrsel), .Rdsel1(Decode_Ctrl_rdsel1), .Rdsel2(Decode_Ctrl_rdsel2), .Clock(clock_1_out),
    .Reg1(registerfile_1_reg1), .Reg2(registerfile_1_reg2));  // open: Clear
  zschwart_DMEMIO_main main_2 (
    .Store_Value(registerfile_1_reg1), .Load_Store_Control(Decode_Ctrl_memwr), .Address(registerfile_1_reg2),
    .Output_Address(main_2_output_address), .Load_Value(main_2_load_value), .Data_Value(main_2_data_value),
    .Write_Control(main_2_write_control), .Clock(clock_2_out));
  Clock clock_2 (.out(clock_2_out));
  LED_Driver_8x8_main main_3 (
    .out_4(main_3_out_4), .out_5(main_3_out_5), .out_6(main_3_out_6), .out_7(main_3_out_7),
    .out_8(main_3_out_8), .out_9(main_3_out_9), .out_10(main_3_out_10), .out_11(main_3_out_11),
    .Data(main_2_data_value), .Address(main_2_output_address), .Write_Control(main_2_write_control));
  ALU_full_section alu_full_section_1 (
    .DataSrc(Decode_Ctrl_datasrc_mux), .DMEM_LB(main_2_load_value), .ALU_OP(Decode_Ctrl_alu_opcode),
    .Register_1(registerfile_1_reg1), .Immediate(Decode_Ctrl_immediate_mux),
    .Register_2(registerfile_1_reg2), .Immediate_Value(Decode_Ctrl_immediate),
    .Branch_Condition(alu_full_section_1_branch_condition),
    .Reg_File_Data_In(alu_full_section_1_reg_file_data_in));
  DotMatrix #(.inputtype("row"), .matrixcols(8), .matrixrows(8)) dotmatrix_1 (
    .row0(main_3_out_4), .row1(main_3_out_5), .row2(main_3_out_6), .row3(main_3_out_7), .row4(main_3_out_8),
    .row5(main_3_out_9), .row6(main_3_out_10), .row7(main_3_out_11));
endmodule
