// Logisim project LED Matrix Example.circ as structural Verilog: 1 circuit, main circuit main
module main (
  input  Data,
  input  [5:0] Address,
  input  Write_Control
);

  wire [7:0] main_1_out_4, main_1_out_5, main_1_out_6, main_1_out_7, main_1_out_8, main_1_out_9,
       main_1_out_10, main_1_out_11;

  LED_Driver_8x8_main main_1 (
    .out_4(main_1_out_4), .out_5(main_1_out_5), .out_6(main_1_out_6), .out_7(main_1_out_7),
    .out_8(main_1_out_8), .out_9(main_1_out_9), .out_10(main_1_out_10), .out_11(main_1_out_11), .Data(Data),
    .Address(Address), .Write_Control(Write_Control));
  DotMatrix #(.inputtype("row"), .matrixcols(8), .matrixrows(8)) dotmatrix_1 (
    .row0(main_1_out_4), .row1(main_1_out_5), .row2(main_1_out_6), .row3(main_1_out_7), .row4(main_1_out_8),
    .row5(main_1_out_9), .row6(main_1_out_10), .row7(main_1_out_11));

  // Notes on the sheet:
  //   To try this out, go to Simulate>Ticks Enabled, or press CTL-K.
  //   This will turn on the global clock signal.  Then, change the inputs to control the matrix.
endmodule
