// Logisim project LED_Driver_8x8.circ as structural Verilog: 2 circuits, main circuit main
module main (
  input  Data,
  input  [5:0] Address,
  input  Write_Control,
  output [7:0] out_4,
  output [7:0] out_5,
  output [7:0] out_6,
  output [7:0] out_7,
  output [7:0] out_8,
  output [7:0] out_9,
  output [7:0] out_10,
  output [7:0] out_11
);

  wire decoder_1_out0, decoder_1_out1, decoder_1_out2, decoder_1_out3, decoder_1_out4, decoder_1_out5,
       decoder_1_out6, decoder_1_out7;
  wire [5:0] divider_1_out, divider_1_rem;

  Divider #(.mode("unsigned"), .width(6)) divider_1 (
    .a(Address), .b(6'b001000), .out(divider_1_out), .rem(divider_1_rem));  // open: upper
  Decoder #(.select(3)) decoder_1 (
    .out0(decoder_1_out0), .out1(decoder_1_out1), .out2(decoder_1_out2), .out3(decoder_1_out3),
    .out4(decoder_1_out4), .out5(decoder_1_out5), .out6(decoder_1_out6), .out7(decoder_1_out7),
    .sel(divider_1_out[2:0]), .en(Write_Control));
  RowStore rowstore_1 (.Output(out_4), .ColAddr(divider_1_rem[2:0]), .Data(Data), .write_Control(decoder_1_out0));
  RowStore rowstore_2 (.Output(out_5), .ColAddr(divider_1_rem[2:0]), .Data(Data), .write_Control(decoder_1_out1));
  RowStore rowstore_3 (.Output(out_6), .ColAddr(divider_1_rem[2:0]), .Data(Data), .write_Control(decoder_1_out2));
  RowStore rowstore_4 (.Output(out_7), .ColAddr(divider_1_rem[2:0]), .Data(Data), .write_Control(decoder_1_out3));
  RowStore rowstore_5 (.Output(out_8), .ColAddr(divider_1_rem[2:0]), .Data(Data), .write_Control(decoder_1_out4));
  RowStore rowstore_6 (.Output(out_9), .ColAddr(divider_1_rem[2:0]), .Data(Data), .write_Control(decoder_1_out5));
  RowStore rowstore_7 (.Output(out_10), .ColAddr(divider_1_rem[2:0]), .Data(Data), .write_Control(decoder_1_out6));
  RowStore rowstore_8 (.Output(out_11), .ColAddr(divider_1_rem[2:0]), .Data(Data), .write_Control(decoder_1_out7));
endmodule

module RowStore (
  input  [2:0] ColAddr,
  input  Data,
  input  write_Control,
  output [7:0] Output
);

  wire clock_1_out;
  wire [7:0] and_1_out, bit_extender_1_out, or_1_out, shifter_1_out, shifter_2_out;

  assign bit_extender_1_out = {{7{1'b0}}, Data};  // Bit_Extender bit_extender_1
  Shifter #(.shift("rl")) shifter_1 (.in(8'hfe), .\dist (ColAddr), .out(shifter_1_out));
  Shifter shifter_2 (.in(bit_extender_1_out), .\dist (ColAddr), .out(shifter_2_out));
  assign and_1_out = {Output[0], Output[1], Output[2], Output[3], Output[4], Output[5], Output[6], Output[7]} & shifter_1_out;  // AND_Gate and_1, 8 bits wide
  assign or_1_out = and_1_out | shifter_2_out;  // OR_Gate or_1, 8 bits wide
  Register RowData (
    .D(or_1_out), .en(write_Control),
    .Q({Output[0], Output[1], Output[2], Output[3], Output[4], Output[5], Output[6], Output[7]}),
    .clk(clock_1_out));  // open: clr
  Clock clock_1 (.out(clock_1_out));
endmodule
