// Logisim project nazhar_PC+IMEM.circ as structural Verilog: 2 circuits, main circuit main
module main (
  input  Branch_Instruction,
  input  [11:0] Jump_Imm_12,
  input  [8:0] Branch_Imm,
  input  JR,
  input  JAL,
  input  Branch_Cond,
  input  [7:0] Reg_1,
  input  Reset_Button,
  output [7:0] Connects_to_the_mux_in_RegFile,
  output [15:0] Connects_to_Decoder
);

  wire and_1_out, Clock_out;
  wire [11:0] adder_2_out, bit_extender_1_out, bit_extender_2_out, multiplexer_1_out, multiplexer_2_out,
       multiplexer_3_out, PC_q;
  wire [11:8] adder_1_out;

  Multiplexer #(.enable("false"), .width(12)) multiplexer_1 (
    .in0(multiplexer_2_out), .in1(bit_extender_1_out), .out(multiplexer_1_out), .sel(JR));
  Clock Clock (.out(Clock_out));
  Multiplexer #(.enable("false"), .width(12)) multiplexer_2 (
    .in0(multiplexer_3_out), .in1(Jump_Imm_12), .out(multiplexer_2_out), .sel(JAL));
  Register #(.width(12)) PC (.D(multiplexer_1_out), .Q(PC_q), .clk(Clock_out), .clr(Reset_Button));  // open: en
  assign bit_extender_1_out = {{4{Reg_1[7]}}, Reg_1};  // Bit_Extender bit_extender_1
  ROM #(.addrWidth(12), .dataWidth(16)) IMEM (.addr(PC_q), .data(Connects_to_Decoder));
  Adder #(.width(12)) adder_1 (
    .a(12'h1), .b(PC_q), .out({adder_1_out, Connects_to_the_mux_in_RegFile}));  // open: cin, cout
  Multiplexer #(.enable("false"), .width(12)) multiplexer_3 (
    .in0({adder_1_out, Connects_to_the_mux_in_RegFile}), .in1(adder_2_out), .out(multiplexer_3_out),
    .sel(and_1_out));
  and and_1 (and_1_out, Branch_Instruction, Branch_Cond);
  assign bit_extender_2_out = {{3{Branch_Imm[8]}}, Branch_Imm};  // Bit_Extender bit_extender_2
  Adder #(.width(12)) adder_2 (.a(bit_extender_2_out), .b(PC_q), .out(adder_2_out));  // open: cin, cout
endmodule

module test (
  input  in_1,
  input  in_2,
  input  in_3,
  input  [11:0] in_4,
  input  [8:0] in_5,
  input  in_6,
  input  [7:0] in_7,
  input  [7:0] in_8,
  input  in_9,
  output [15:0] out_10
);

  Clock clock_1 ();  // open: out
  // main main_1: pin names not known; wires that end beside it: in_1, in_4, in_5, in_2, in_3, in_6, in_7, in_8, in_9, out_10
endmodule
