// Logisim project she_decode_control.circ as structural Verilog: 2 circuits, main circuit main
module main (
  input  [15:0] Data,
  output DataSrc_Mux,
  output MemWr,
  output WrCtrl,
  output Branch_Instr,
  output Immediate_Mux,
  output [2:0] ALU_Opcode,
  output JR,
  output JAL,
  output [11:0] JumpImm,
  output [2:0] WrSel,
  output [2:0] Rdsel1,
  output [8:0] Branch_Imm,
  output [2:0] Rdsel2,
  output [7:0] Immediate
);

  wire decoder_1_out0, decoder_1_out2, decoder_1_out3, decoder_1_out4, decoder_1_out5, decoder_1_out6,
       decoder_1_out7, decoder_1_out8, decoder_1_out9;

  Decoder #(.select(4)) decoder_1 (
    .out0(decoder_1_out0), .out1(MemWr), .out2(decoder_1_out2), .out3(decoder_1_out3), .out4(decoder_1_out4),
    .out5(decoder_1_out5), .out6(decoder_1_out6), .out7(decoder_1_out7), .out8(decoder_1_out8),
    .out9(decoder_1_out9), .out10(JR), .out11(JAL), .sel(Data[15:12]), .en(1'b1));  // open: out12, out13, out14, out15
  or or_1 (Branch_Instr, decoder_1_out7, decoder_1_out8, decoder_1_out9);
  Multiplexer #(.enable("false"), .width(3)) multiplexer_1 (.in0(Data[11:9]), .in1(3'b111), .out(WrSel), .sel(JAL));
  or or_2 (Immediate_Mux, decoder_1_out5, decoder_1_out6);
  not not_1 (DataSrc_Mux, decoder_1_out0);
  Multiplexer #(.enable("false"), .width(3)) multiplexer_2 (
    .in0(Data[8:6]), .in1(Data[11:9]), .out(Rdsel1), .sel(Immediate_Mux));
  or or_3 (ALU_Opcode[1], decoder_1_out4, decoder_1_out6, decoder_1_out9);
  or msb (ALU_Opcode[2], decoder_1_out6, decoder_1_out8, decoder_1_out7);
  or lsb (ALU_Opcode[0], decoder_1_out3, decoder_1_out8, decoder_1_out9);
  Multiplexer #(.enable("false"), .width(3)) multiplexer_3 (
    .in0(Data[5:3]), .in1(3'b110), .out(Rdsel2), .sel(Branch_Instr));
  or or_4 (WrCtrl, decoder_1_out0, decoder_1_out2, decoder_1_out3, decoder_1_out4, decoder_1_out5, decoder_1_out6, JAL);

  assign Branch_Imm = Data[8:0];
  assign Immediate = Data[7:0];
  assign JumpImm = Data[11:0];

  // Notes on the sheet:
  //   4 bit opcode
  //   12 bit jumpImm
  //   dest
  //   lb
  //   sb
  //   add
  //   sub
  //   move
  //   addi
  //   seti
  //   9 bit immediate for branching
  //   8 bit immediate for addi, seti
endmodule

module testing (
  input  [15:0] in_1,
  output out_2,
  output out_3,
  output out_4,
  output out_5,
  output out_6,
  output out_7,
  output out_8,
  output [2:0] out_9,
  output [11:0] out_10,
  output [2:0] out_11,
  output [8:0] out_12,
  output [2:0] out_13,
  output [2:0] out_14,
  output [7:0] out_15
);

  main main_1 (
    .Data(in_1), .DataSrc_Mux(out_2), .MemWr(out_3), .WrCtrl(out_4), .Branch_Instr(out_5),
    .Immediate_Mux(out_6), .JR(out_7), .JAL(out_8), .ALU_Opcode(out_9), .JumpImm(out_10), .WrSel(out_11),
    .Branch_Imm(out_12), .Rdsel1(out_13), .Rdsel2(out_14), .Immediate(out_15));
endmodule
