// Logisim project tkomatsu_ALU.circ as structural Verilog: 3 circuits, main circuit ALU
module ALU (
  input  [2:0] ALU_OP,
  input  [7:0] SRC1,
  input  [7:0] SRC2,
  output [7:0] OUT
);

  wire bne_helper_1_output, not_1_out;
  wire [7:0] adder_1_out, bit_extender_1_out, bit_extender_2_out, bit_extender_3_out, subtractor_1_out,
       xnor_1_out;

  Adder adder_1 (.a(SRC1), .b(SRC2), .out(adder_1_out));  // open: cin, cout
  Subtractor subtractor_1 (.a(SRC1), .b(SRC2), .out(subtractor_1_out));  // open: bin, bout
  assign xnor_1_out = ~(subtractor_1_out ^ 8'h80);  // XNOR_Gate xnor_1, 8 bits wide
  not not_1 (not_1_out, bne_helper_1_output);
  BNE_Helper bne_helper_1 (.Output(bne_helper_1_output), .Input(subtractor_1_out));
  assign bit_extender_1_out = {{7{1'b0}}, xnor_1_out[7]};  // Bit_Extender bit_extender_1
  assign bit_extender_2_out = {{7{1'b0}}, not_1_out};  // Bit_Extender bit_extender_2
  assign bit_extender_3_out = {{7{1'b0}}, bne_helper_1_output};  // Bit_Extender bit_extender_3
  Multiplexer #(.enable("false"), .select(3), .width(8)) multiplexer_1 (
    .in0(adder_1_out), .in1(subtractor_1_out), .in2(SRC1), .in3(bit_extender_1_out),
    .in4(bit_extender_2_out), .in5(bit_extender_3_out), .in6(SRC2), .out(OUT), .sel(ALU_OP));  // open: in7
endmodule

module BNE_Helper (
  input  [7:0] Input,
  output Output
);

  wire or_1_out, or_2_out, or_3_out, or_4_out, or_5_out, or_6_out;

  or or_1 (or_1_out, Input[6], Input[7]);
  or or_2 (or_2_out, Input[5], or_1_out);
  or or_3 (or_3_out, Input[4], or_2_out);
  or or_4 (or_4_out, Input[3], or_3_out);
  or or_5 (or_5_out, Input[2], or_4_out);
  or or_6 (or_6_out, Input[1], or_5_out);
  or or_7 (Output, Input[0], or_6_out);
endmodule

module ALU_full_section (
  input  DataSrc,
  input  [7:0] DMEM_LB,
  input  [2:0] ALU_OP,
  input  [7:0] Register_1,
  input  Immediate,
  input  [7:0] Register_2,
  input  [7:0] Immediate_Value,
  output Branch_Condition,
  output [7:0] Reg_File_Data_In
);

  wire [7:0] multiplexer_1_out;
  wire [7:1] alu_1_out;

  Multiplexer #(.enable("false"), .width(8)) multiplexer_1 (
    .in0(Register_2), .in1(Immediate_Value), .out(multiplexer_1_out), .sel(Immediate));
  Multiplexer #(.enable("false"), .width(8)) multiplexer_2 (
    .in0(DMEM_LB), .in1({alu_1_out, Branch_Condition}), .out(Reg_File_Data_In), .sel(DataSrc));
  ALU alu_1 (.ALU_OP(ALU_OP), .SRC1(Register_1), .SRC2(multiplexer_1_out), .OUT({alu_1_out, Branch_Condition}));
endmodule
