// Logisim project tlahey_registerfile.circ as structural Verilog: 4 circuits, main circuit registerfile
module registerfile (
  input  [7:0] ALU_DMEM_Input,
  input  [7:0] JAL_PC_input,
  input  JAL,
  input  Wrctl,
  input  [2:0] Wrsel,
  input  [2:0] Rdsel1,
  input  [2:0] Rdsel2,
  input  Clock,
  input  Clear,
  output [7:0] Reg1,
  output [7:0] Reg2
);

  wire demultiplexer_2_out0, demultiplexer_2_out1, demultiplexer_2_out2, demultiplexer_2_out3,
       demultiplexer_2_out4, demultiplexer_2_out5, demultiplexer_2_out6, demultiplexer_2_out7;
  wire [7:0] demultiplexer_1_out0, demultiplexer_1_out1, demultiplexer_1_out2, demultiplexer_1_out3,
       demultiplexer_1_out4, demultiplexer_1_out5, demultiplexer_1_out6, demultiplexer_1_out7,
       multiplexer_1_out, register_1_q, register_2_q, register_3_q, register_4_q, register_5_q, register_6_q,
       register_7_q, register_8_q;

  Multiplexer #(.enable("false"), .width(8)) multiplexer_1 (
    .in0(ALU_DMEM_Input), .in1(JAL_PC_input), .out(multiplexer_1_out), .sel(JAL));
  Demultiplexer #(.enable("false"), .select(3), .width(8)) demultiplexer_1 (
    .out0(demultiplexer_1_out0), .out1(demultiplexer_1_out1), .out2(demultiplexer_1_out2),
    .out3(demultiplexer_1_out3), .out4(demultiplexer_1_out4), .out5(demultiplexer_1_out5),
    .out6(demultiplexer_1_out6), .out7(demultiplexer_1_out7), .in(multiplexer_1_out), .sel(Wrsel));
  Demultiplexer #(.enable("false"), .select(3)) demultiplexer_2 (
    .out0(demultiplexer_2_out0), .out1(demultiplexer_2_out1), .out2(demultiplexer_2_out2),
    .out3(demultiplexer_2_out3), .out4(demultiplexer_2_out4), .out5(demultiplexer_2_out5),
    .out6(demultiplexer_2_out6), .out7(demultiplexer_2_out7), .in(Wrctl), .sel(Wrsel));
  Register register_1 (.D(demultiplexer_1_out0), .en(demultiplexer_2_out0), .Q(register_1_q), .clk(Clock), .clr(Clear));
  Register register_2 (.D(demultiplexer_1_out1), .en(demultiplexer_2_out1), .Q(register_2_q), .clk(Clock), .clr(Clear));
  Register register_3 (.D(demultiplexer_1_out2), .en(demultiplexer_2_out2), .Q(register_3_q), .clk(Clock), .clr(Clear));
  Register register_4 (.D(demultiplexer_1_out3), .en(demultiplexer_2_out3), .Q(register_4_q), .clk(Clock), .clr(Clear));
  Register register_5 (.D(demultiplexer_1_out4), .en(demultiplexer_2_out4), .Q(register_5_q), .clk(Clock), .clr(Clear));
  Register register_6 (.D(demultiplexer_1_out5), .en(demultiplexer_2_out5), .Q(register_6_q), .clk(Clock), .clr(Clear));
  Register register_7 (.D(demultiplexer_1_out6), .en(demultiplexer_2_out6), .Q(register_7_q), .clk(Clock), .clr(Clear));
  Register register_8 (.D(demultiplexer_1_out7), .en(demultiplexer_2_out7), .Q(register_8_q), .clk(Clock), .clr(Clear));
  Multiplexer #(.enable("false"), .select(3), .width(8)) multiplexer_2 (
    .in0(register_1_q), .in1(register_2_q), .in2(register_3_q), .in3(register_4_q), .in4(register_5_q),
    .in5(register_6_q), .in6(register_7_q), .in7(register_8_q), .out(Reg1), .sel(Rdsel1));
  Multiplexer #(.enable("false"), .select(3), .width(8)) multiplexer_3 (
    .in0(register_1_q), .in1(register_2_q), .in2(register_3_q), .in3(register_4_q), .in4(register_5_q),
    .in5(register_6_q), .in6(register_7_q), .in7(register_8_q), .out(Reg2), .sel(Rdsel2));

  // Notes on the sheet:
  //   Data In
endmodule

module register (
);

  Register register_1 ();  // open: D, en, Q, clk, clr
endmodule

module d_flip_flop (
  input  Clock,
  input  Data_In,
  output Data_Out
);

  wire and_1_out, not_1_out, not_2_out, not_3_out;

  not not_1 (not_1_out, Clock);
  not not_2 (not_2_out, not_1_out);
  not not_3 (not_3_out, not_2_out);
  and and_1 (and_1_out, Clock, not_3_out);
  d_latch d_latch_1 (.Clock(and_1_out), .Data_In(Data_In), .Data_Out(Data_Out));
endmodule

module d_latch (
  input  Clock,
  input  Data_In,
  output Data_Out
);

  wire and_1_out, and_2_out, nor_1_out, not_1_out;

  not not_1 (not_1_out, Data_In);
  and and_1 (and_1_out, Clock, not_1_out);
  buf and_2 (and_2_out, Data_In);  // AND_Gate
  nor nor_1 (nor_1_out, and_2_out, Data_Out);
  nor nor_2 (Data_Out, and_1_out, nor_1_out);
endmodule
