// Logisim project zschwart_DMEMIO.circ as structural Verilog: 1 circuit, main circuit main
module main (
  input  [7:0] Store_Value,
  input  Load_Store_Control,
  input  Clock,
  input  [7:0] Address,
  output [5:0] Output_Address,
  output [7:0] Load_Value,
  output Data_Value,
  output Write_Control
);

  wire not_1_out;
  wire [2:1] bit_extender_2_out;
  wire [6:0] demultiplexer_1_out0, demultiplexer_1_out1;

  Demultiplexer #(.enable("false"), .width(7)) demultiplexer_1 (
    .out0(demultiplexer_1_out0), .out1(demultiplexer_1_out1), .in(Address[6:0]), .sel(Address[7]));
  not not_1 (not_1_out, Load_Store_Control);
  Bit_Extender #(.in_width(7), .out_width(6)) bit_extender_1 (.in(demultiplexer_1_out1), .out(Output_Address));
  Bit_Extender #(.out_width(3)) bit_extender_2 (.in(Store_Value), .out({bit_extender_2_out, Data_Value}));
  and and_1 (Write_Control, Address[7], Load_Store_Control);
  assign Load_Value = Load_Store_Control ? Store_Value : 8'bz;  // Controlled_Buffer controlled_buffer_1
  RAM #(.addrWidth(7), .databus("bidir")) ram_1 (.addr(demultiplexer_1_out0), .data(Load_Value));  // open: we, oe, clk
endmodule
